// Logisim project sequential-digital-systems-logisim.circ as structural Verilog: 19 circuits, main circuit SR_Latch
module SR_Latch (
  input  R,
  input  S,
  output Q,
  output notQ
);

  nor nor_1 (Q, R, notQ);
  nor nor_2 (notQ, Q, S);
endmodule

module SR_LatchClock (
  input  R,
  input  C,
  input  S,
  output Q,
  output notQ
);

  wire and_1_out, and_2_out;

  and and_1 (and_1_out, R, C);
  and and_2 (and_2_out, C, S);
  SR_Latch sr_latch_1 (.R(and_1_out), .S(and_2_out), .Q(Q), .notQ(notQ));
endmodule

module D_Latch (
  input  D,
  input  Clk,
  output Q,
  output NotQ
);

  wire not_1_out;

  not not_1 (not_1_out, D);
  SR_LatchClock sr_latchclock_1 (.R(not_1_out), .C(Clk), .S(D), .Q(Q), .notQ(NotQ));
endmodule

module D_FlipFlop (
  input  D,
  input  Clk,
  output Q,
  output NotQ
);

  wire d_latch_1_q, not_1_out, not_2_out;

  not not_1 (not_1_out, Clk);
  D_Latch d_latch_1 (.D(D), .Clk(not_1_out), .Q(d_latch_1_q));  // open: NotQ
  not not_2 (not_2_out, not_1_out);
  D_Latch d_latch_2 (.D(d_latch_1_q), .Clk(not_2_out), .Q(Q), .NotQ(NotQ));
endmodule

module D_FLipFlopReset (
  input  D,
  input  Clk,
  input  RST,
  output Q,
  output NotQ
);

  wire and_1_out, not_1_out;

  not not_1 (not_1_out, RST);
  and and_1 (and_1_out, D, not_1_out);
  D_FlipFlop d_flipflop_1 (.D(and_1_out), .Clk(Clk), .Q(Q), .NotQ(NotQ));
endmodule

module D_FlipFLopTest (
  output Q,
  output notQ
);

  wire Clk_out, D_out, RST_out;

  Clock #(.highDuration(2), .lowDuration(2)) D (.out(D_out));
  Clock Clk (.out(Clk_out));
  Clock #(.highDuration(4), .lowDuration(4)) RST (.out(RST_out));
  D_FLipFlopReset d_flipflopreset_1 (.D(D_out), .Clk(Clk_out), .RST(RST_out), .Q(Q), .NotQ(notQ));
endmodule

module SRLatch (
  input  R,
  input  Clk,
  input  S,
  output Q,
  output Qnot
);

  wire and_1_out, and_2_out;

  and and_1 (and_1_out, R, Clk);
  and and_2 (and_2_out, Clk, S);
  nor nor_1 (Q, and_1_out, Qnot);
  nor nor_2 (Qnot, Q, and_2_out);
endmodule

module RSLatchReset (
  input  Reset,
  input  R,
  input  Clk,
  input  S,
  output Q,
  output Qnot
);

  wire and_1_out, and_2_out, or_1_out;

  and and_1 (and_1_out, R, ~Reset, Clk);  // AND_Gate
  and and_2 (and_2_out, Clk, ~Reset, S);  // AND_Gate
  or or_1 (or_1_out, Reset, and_1_out);
  nor nor_1 (Q, or_1_out, Qnot);
  nor nor_2 (Qnot, Q, and_2_out);
endmodule

module JkAsynchronous (
  input  Reset,
  input  K,
  input  J,
  input  Clk,
  output Q,
  output Qnot
);

  wire and_1_out, and_2_out, not_1_out, rslatchreset_1_q, rslatchreset_1_qnot;

  and and_1 (and_1_out, Q, K);
  and and_2 (and_2_out, J, Qnot);
  not not_1 (not_1_out, Clk);
  RSLatchReset rslatchreset_1 (
    .Reset(Reset), .R(and_1_out), .Clk(Clk), .S(and_2_out), .Q(rslatchreset_1_q), .Qnot(rslatchreset_1_qnot));
  RSLatchReset rslatchreset_2 (
    .Reset(Reset), .R(rslatchreset_1_qnot), .Clk(not_1_out), .S(rslatchreset_1_q), .Q(Q), .Qnot(Qnot));
endmodule

module JkAnalysis (
);

  wire Clk_out, J_out, jkasynchronous_1_q, jkasynchronous_1_qnot, K_out, Reset_out;

  Clock Clk (.out(Clk_out));
  Clock #(.highDuration(2), .lowDuration(2)) J (.out(J_out));
  Clock #(.highDuration(4), .lowDuration(4)) K (.out(K_out));
  Clock #(.highDuration(16), .lowDuration(16)) Reset (.out(Reset_out));
  JkAsynchronous jkasynchronous_1 (
    .Reset(Reset_out), .K(K_out), .J(J_out), .Clk(Clk_out), .Q(jkasynchronous_1_q),
    .Qnot(jkasynchronous_1_qnot));
  LED Q (.in(jkasynchronous_1_q));
  LED Qnot (.in(jkasynchronous_1_qnot));
endmodule

module ShiftRegister (
  input  SHIFT,
  input  LOAD,
  input  SI,
  input  PI,
  input  CLK,
  input  RESET,
  output out_7
);

  wire and_1_out, and_2_out, and_3_out, not_1_out, not_2_out, or_1_out;

  not not_1 (not_1_out, SHIFT);
  not not_2 (not_2_out, LOAD);
  and and_1 (and_1_out, SI, SHIFT);
  and and_2 (and_2_out, PI, not_1_out, LOAD);
  and and_3 (and_3_out, not_1_out, not_2_out, out_7);
  or or_1 (or_1_out, and_1_out, and_2_out, and_3_out);
  D_FLipFlopReset d_flipflopreset_1 (.D(or_1_out), .Clk(CLK), .RST(RESET), .Q(out_7));  // open: NotQ
endmodule

module ShiftRegister4bit (
  input  SHIFT,
  input  LOAD,
  input  SI,
  input  PI1,
  input  PI2,
  input  PI3,
  input  PI4,
  input  CLK,
  input  RESET,
  output B1,
  output B2,
  output B3,
  output B4
);

  ShiftRegister shiftregister_1 (.SHIFT(SHIFT), .LOAD(LOAD), .SI(SI), .PI(PI1), .CLK(CLK), .RESET(RESET), .out_7(B1));
  ShiftRegister shiftregister_2 (.SHIFT(SHIFT), .LOAD(LOAD), .SI(B1), .PI(PI2), .CLK(CLK), .RESET(RESET), .out_7(B2));
  ShiftRegister shiftregister_3 (.SHIFT(SHIFT), .LOAD(LOAD), .SI(B2), .PI(PI3), .CLK(CLK), .RESET(RESET), .out_7(B3));
  ShiftRegister shiftregister_4 (.SHIFT(SHIFT), .LOAD(LOAD), .SI(B3), .PI(PI4), .CLK(CLK), .RESET(RESET), .out_7(B4));
endmodule

module ShiftRegister4bitClocks (
  input  LOAD,
  input  PI1,
  input  PI2,
  input  PI3,
  input  PI4,
  input  RESET,
  output B1,
  output B2,
  output B3,
  output B4
);

  wire CLK_out, SHIFT_out, SI_out;

  Clock #(.phaseOffset(1)) SHIFT (.out(SHIFT_out));
  Clock #(.highDuration(8), .lowDuration(8)) SI (.out(SI_out));
  Clock CLK (.out(CLK_out));
  ShiftRegister shiftregister_1 (
    .SHIFT(SHIFT_out), .LOAD(LOAD), .SI(SI_out), .PI(PI1), .CLK(CLK_out), .RESET(RESET), .out_7(B1));
  ShiftRegister shiftregister_2 (
    .SHIFT(SHIFT_out), .LOAD(LOAD), .SI(B1), .PI(PI2), .CLK(CLK_out), .RESET(RESET), .out_7(B2));
  ShiftRegister shiftregister_3 (
    .SHIFT(SHIFT_out), .LOAD(LOAD), .SI(B2), .PI(PI3), .CLK(CLK_out), .RESET(RESET), .out_7(B3));
  ShiftRegister shiftregister_4 (
    .SHIFT(SHIFT_out), .LOAD(LOAD), .SI(B3), .PI(PI4), .CLK(CLK_out), .RESET(RESET), .out_7(B4));
endmodule

module Sequence_Detector (
  input  X0,
  input  X1,
  input  Clk,
  input  RST,
  output Z
);

  wire A_notq, A_q, and_1_out, and_2_out, and_3_out, and_4_out, and_5_out, and_6_out, and_7_out, B_notq, B_q,
       or_1_out, or_2_out;

  and and_1 (and_1_out, X0, B_q, X1);
  and and_2 (and_2_out, B_q, A_q, X0, X1);
  and and_3 (and_3_out, ~X0, ~X1);  // AND_Gate
  and and_4 (and_4_out, B_q, A_notq, X0, X1);
  and and_5 (and_5_out, A_q, B_notq, X0, X1);
  and and_6 (and_6_out, B_notq, A_q, X0, X1);
  and and_7 (and_7_out, B_q, A_notq, X0, X1);
  or or_1 (or_1_out, and_1_out, and_2_out);
  or or_2 (or_2_out, and_3_out, and_4_out, and_5_out);
  or or_3 (Z, and_6_out, and_7_out);
  D_FLipFlopReset A (.D(or_1_out), .Clk(Clk), .RST(RST), .Q(A_q), .NotQ(A_notq));
  D_FLipFlopReset B (.D(or_2_out), .Clk(Clk), .RST(RST), .Q(B_q), .NotQ(B_notq));
endmodule

module Sequence_Detector_test (
  output out_1
);

  wire Clk_out, RST_out, X0_out, X1_out;

  Clock X0 (.out(X0_out));
  Clock #(.highDuration(2), .lowDuration(2)) X1 (.out(X1_out));
  Clock #(.lowDuration(4)) Clk (.out(Clk_out));
  Clock #(.highDuration(8), .lowDuration(8)) RST (.out(RST_out));
  Sequence_Detector sequence_detector_1 (.X0(X0_out), .X1(X1_out), .Clk(Clk_out), .RST(RST_out), .Z(out_1));
endmodule

module Serial_Adder (
  input  SHIFT,
  input  LOAD,
  input  PI0_1,
  input  PI0_2,
  input  PI0_3,
  input  PI0_4,
  input  RESET_A,
  input  SI,
  input  PI1_1,
  input  PI1_2,
  input  PI1_3,
  input  PI1_4,
  output B0_1,
  output B0_2,
  output B0_3,
  output B0_4,
  output B1_1,
  output B1_2,
  output B1_3,
  output B1_4
);

  wire CLK_out, d_flipflopreset_1_q, fulladder_1_carry, fulladder_1_sum;

  Clock CLK (.out(CLK_out));
  ShiftRegister4bit shiftregister4bit_1 (
    .SHIFT(SHIFT), .LOAD(LOAD), .SI(fulladder_1_sum), .PI1(PI0_1), .PI2(PI0_2), .PI3(PI0_3), .PI4(PI0_4),
    .CLK(CLK_out), .RESET(RESET_A), .B1(B0_1), .B2(B0_2), .B3(B0_3), .B4(B0_4));
  ShiftRegister4bit shiftregister4bit_2 (
    .SHIFT(SHIFT), .LOAD(LOAD), .SI(SI), .PI1(PI1_1), .PI2(PI1_2), .PI3(PI1_3), .PI4(PI1_4), .CLK(CLK_out),
    .RESET(RESET_A), .B1(B1_1), .B2(B1_2), .B3(B1_3), .B4(B1_4));
  FullAdder fulladder_1 (
    .InputC(B0_4), .InputA(B1_4), .InputB(d_flipflopreset_1_q), .Sum(fulladder_1_sum),
    .Carry(fulladder_1_carry));
  D_FLipFlopReset d_flipflopreset_1 (
    .D(fulladder_1_carry), .Clk(CLK_out), .RST(RESET_A), .Q(d_flipflopreset_1_q));  // open: NotQ

  // Notes on the sheet:
  //   -------most significant
  //   --------least significant
  //   -----most significant
  //   -----least significant
endmodule

module HalfAdder (
  input  InputA,
  input  InputB,
  output Sum,
  output Carry
);

  xor xor_1 (Sum, InputA, InputB);
  and and_1 (Carry, InputA, InputB);
endmodule

module FullAdder (
  input  InputC,
  input  InputA,
  input  InputB,
  output Sum,
  output Carry
);

  wire halfadder_1_carry, halfadder_1_sum, halfadder_2_carry;

  HalfAdder halfadder_1 (.InputA(InputA), .InputB(InputB), .Sum(halfadder_1_sum), .Carry(halfadder_1_carry));
  HalfAdder halfadder_2 (.InputA(InputC), .InputB(halfadder_1_sum), .Sum(Sum), .Carry(halfadder_2_carry));
  or or_1 (Carry, halfadder_2_carry, halfadder_1_carry);
endmodule

module Serial_Adder_test (
  input  SHIFT,
  input  LOAD,
  input  PI0_1,
  input  PI0_2,
  input  PI0_3,
  input  PI0_4,
  input  RESET_A,
  input  SI,
  input  PI1_1,
  input  PI1_2,
  input  PI1_3,
  input  PI1_4,
  output B0_1,
  output B0_2,
  output B0_3,
  output B0_4,
  output B1_1,
  output B1_2,
  output B1_3,
  output B1_4
);

  wire CLK_out, d_flipflopreset_1_q, fulladder_1_carry, fulladder_1_sum;

  Clock CLK (.out(CLK_out));
  ShiftRegister4bit shiftregister4bit_1 (
    .SHIFT(SHIFT), .LOAD(LOAD), .SI(fulladder_1_sum), .PI1(PI0_1), .PI2(PI0_2), .PI3(PI0_3), .PI4(PI0_4),
    .CLK(CLK_out), .RESET(RESET_A), .B1(B0_1), .B2(B0_2), .B3(B0_3), .B4(B0_4));
  ShiftRegister4bit shiftregister4bit_2 (
    .SHIFT(SHIFT), .LOAD(LOAD), .SI(SI), .PI1(PI1_1), .PI2(PI1_2), .PI3(PI1_3), .PI4(PI1_4), .CLK(CLK_out),
    .RESET(RESET_A), .B1(B1_1), .B2(B1_2), .B3(B1_3), .B4(B1_4));
  FullAdder fulladder_1 (
    .InputC(B0_4), .InputA(B1_4), .InputB(d_flipflopreset_1_q), .Sum(fulladder_1_sum),
    .Carry(fulladder_1_carry));
  D_FLipFlopReset d_flipflopreset_1 (
    .D(fulladder_1_carry), .Clk(CLK_out), .RST(RESET_A), .Q(d_flipflopreset_1_q));  // open: NotQ

  // Notes on the sheet:
  //   -------most significant
  //   --------least significant
  //   -----most significant
  //   -----least significant
endmodule
